// Logisim project main.circ as structural Verilog: 11 circuits, main circuit main
module main (
);

  wire adder_1_out, and_1_out, and_7_out, and_10_out, and_11_out, and_12_out, and_13_out, and_14_out,
       and_15_out, and_16_out, and_17_out, and_18_out, and_19_out, and_20_out, and_21_out, and_22_out,
       and_23_out, and_24_out, and_25_out, and_26_out, and_27_out, and_28_out, and_29_out, and_30_out,
       and_33_out, and_34_out, and_35_out, and_36_out, and_37_out, and_38_out, and_39_out, and_40_out,
       and_41_out, and_43_out, ATCenMove, ATCenMoved, ATCinisW, ATCinit, ATCInpFlpre, ATCnEhp, ATCnewENclc,
       ATCuncorrectInp, buffer_4_out, button_1_out, button_2_out, changePCx, changePCy, chGM, CHHPinmove,
       clock_1_out, comparator_1_eq, comparator_2_eq, comparator_3_eq, comparator_4_eq, comparator_5_eq,
       comparator_6_eq, comparator_7_eq, comparator_8_eq, comparator_9_eq, comparator_10_eq,
       comparator_11_eq, comparator_11_gt, comparator_11_lt, comparator_12_eq, comparator_12_lt,
       comparator_13_eq, comparator_14_lt, comparator_15_gt, comparator_16_lt, comparator_17_gt,
       comparator_18_lt, comparator_19_gt, comparator_20_lt, comparator_21_gt, comparator_22_lt,
       comparator_23_gt, comparator_24_lt, comparator_26_lt, comparator_27_gt, comparator_28_lt,
       comparator_29_gt, comparator_30_eq, comparator_31_eq, comparator_32_eq, comparator_33_eq,
       comparator_34_eq, comparator_35_eq, comparator_36_eq, comparator_37_eq, comparator_38_eq,
       comparator_39_eq, comparator_39_gt, comparator_39_lt, comparator_40_eq, comparator_41_eq,
       comparator_42_eq, comparator_43_eq, comparator_44_eq, comparator_45_eq, comparator_46_eq,
       comparator_47_eq, comparator_48_eq, comparator_49_eq, comparator_50_eq, comparator_51_eq,
       comparator_52_eq, comparator_53_eq, comparator_54_eq, comparator_55_eq, comparator_56_eq,
       comparator_57_eq, comparator_58_eq, comparator_59_eq, comparator_60_eq, comparator_61_eq,
       comparator_62_lt, comparator_63_gt, comparator_64_lt, comparator_65_gt, comparator_66_lt,
       comparator_67_gt, comparator_68_lt, comparator_69_gt, comparator_70_lt, comparator_71_gt,
       comparator_72_lt, comparator_73_eq, comparator_74_eq, comparator_75_eq, comparator_76_eq,
       comparator_77_gt, comparator_78_gt, comparator_79_gt, comparator_80_gt, comparator_81_lt,
       comparator_82_lt, comparator_83_lt, comparator_84_lt, comparator_85_eq, comparator_86_eq,
       comparator_87_eq, comparator_89_eq, CONSOLE_PRINTER_connected, CONSOLE_PRINTER_it_worked,
       demultiplexer_1_out1, demultiplexer_3_out0, demultiplexer_3_out1, demultiplexer_3_out2,
       demultiplexer_3_out3, demultiplexer_4_out0, demultiplexer_4_out1, demultiplexer_4_out2, gS0, gS1, gS2,
       InpFl1, InpFl2, InpFlmove1, InpFlmove2, InpFlmove31, InpFlmove32, InpFlmove33, InpFlmove34,
       InpFlmove35, InpFlpre, InpFlpreAtc, InpFlpreSTRT, \InpFlpreС , INV1ch, INV2ch, INV3ch, INV4ch, INV5ch,
       invchn, ITEMinCELL, itemRES1, itemRES2, itemRES3, itemRES4, itemRES5, letsPrint, LoadMap, mainClk,
       mainRES, MapLevelCh, mapPREst, mapPREst1, memReadyToPrint, not_1_out, not_2_out, not_3_out, not_4_out,
       not_5_out, not_6_out, not_7_out, not_8_out, not_9_out, not_10_out, not_11_out, not_12_out, not_13_out,
       not_14_out, not_15_out, or_1_out, or_2_out, or_3_out, or_4_out, or_5_out, or_6_out, or_7_out,
       or_8_out, or_9_out, or_11_out, or_12_out, or_16_out, or_18_out, or_19_out, or_20_out, or_21_out,
       or_23_out, or_24_out, or_25_out, or_31_out, or_33_out, or_34_out, or_35_out, PLAYERHPCH, PlDirCh,
       pull_resistor_2_node, pull_resistor_3_node, pull_resistor_5_node, pull_resistor_7_node,
       pull_resistor_8_node, qres, quick_1_out, quick_7_out, quick_8_out, quick_16_out, quick_17_out,
       quick_23_out, quick_27_out, quick_28_out, random_1_out, register_6_q, register_7_q, StateCh, stMapCLC,
       stMapCLC1, stMapCLC2, TOPRINTRES, WonInp;
  wire [1:0] adder_13_out, ATCcurEN, ATCnewEN, bit_extender_4_out, bit_extender_5_out, bit_extender_6_out,
       bit_extender_7_out, gameState, gSto, NewPlDir, PlDir, subtractor_15_out;
  wire [2:0] adder_9_out, bit_extender_1_out, bit_extender_3_out, register_31_q;
  wire [3:0] adder_4_out, register_13_q;
  wire [7:0] adder_2_out, adder_3_out, adder_5_out, adder_6_out, adder_7_out, adder_8_out, adder_10_out,
       adder_12_out, ATCInpKey, bit_extender_2_out, ENDMG, ENDMGst, enemies_1_hp, ENHP, ENHPst, ENimgChrst,
       ENIMN, ENNmChrst, food_1_givehp, gStdtScrMem, InpKey, InpKeyall, INVENTORY1, INVENTORY1p, INVENTORY2,
       INVENTORY2p, INVENTORY3, INVENTORY3p, INVENTORY4, INVENTORY4p, INVENTORY5, INVENTORY5p, LENHP,
       mapLevelCur, maps_1_xpp, maps_1_ypp, mapSTDATAreaded, memChar, multiplexer_1_out, multiplexer_2_out,
       multiplexer_3_out, multiplexer_4_out, multiplexer_7_out, multiplexer_8_out, NewMapLevelCh,
       NewPlayerHP, NewPLxOM, NewPLyOM, objectONmap, p__y_2, p_x_1_y, p_x_1_y_t, p_x_2_y, p_x_2_y_t, p_x_y,
       p_x_y_1, p_x_y_1_t, p_x_y_2, playerHPCUR, PLxOM, PLyOM, subtractor_1_out, subtractor_2_out,
       subtractor_3_out, subtractor_4_out, subtractor_5_out, subtractor_6_out, subtractor_7_out,
       subtractor_8_out, subtractor_9_out, subtractor_10_out, subtractor_11_out, subtractor_12_out,
       subtractor_13_out, subtractor_14_out, weapon_1_dmg;
  wire [11:0] adder_11_out, MAP_tospace_ELEM, MapH, maps_1_height, maps_1_width, mapSTelemREAD, MapW, memN,
       multiplexer_5_out, p_x_1_y__elemOnMap, p_x_1_y__elemOnMap_t, p_x_2_y__elemOnMap, p_x_2_y__elemOnMap_t,
       p_x_y_1__elemOnMap, p_x_y_1__elemOnMap_t, p_x_y_2__elemOnMap, p_x_y_2__elemOnMap_t, p_x_y__elemOnMap,
       tpLen;

  Comparator comparator_1 (.a(InpKey), .b(8'h31), .eq(comparator_1_eq));  // open: gt, lt
  Comparator comparator_2 (.a(InpKey), .b(8'h32), .eq(comparator_2_eq));  // open: gt, lt
  Comparator comparator_3 (.a(InpKey), .b(8'h33), .eq(comparator_3_eq));  // open: gt, lt
  Comparator comparator_4 (.a(InpKey), .b(8'h34), .eq(comparator_4_eq));  // open: gt, lt
  Comparator comparator_5 (.a(InpKey), .b(8'h35), .eq(comparator_5_eq));  // open: gt, lt
  Register register_1 (.D(p_x_y), .Q(INVENTORY1), .clk(INV1ch), .clr(or_1_out));  // open: en
  or or_1 (or_1_out, mainRES, itemRES1);
  Register register_2 (.D(p_x_y), .Q(INVENTORY2), .clk(INV2ch), .clr(or_2_out));  // open: en
  or or_2 (or_2_out, mainRES, itemRES2);
  Register register_3 (.D(p_x_y), .Q(INVENTORY3), .clk(INV3ch), .clr(or_3_out));  // open: en
  or or_3 (or_3_out, mainRES, itemRES3);
  Register register_4 (.D(p_x_y), .Q(INVENTORY4), .clk(INV4ch), .clr(or_4_out));  // open: en
  or or_4 (or_4_out, mainRES, itemRES4);
  Register register_5 (.D(p_x_y), .Q(INVENTORY5), .clk(INV5ch), .clr(or_5_out));  // open: en
  or or_5 (or_5_out, mainRES, itemRES5);
  Comparator comparator_6 (.a(InpKeyall), .b(8'h31), .eq(comparator_6_eq));  // open: gt, lt
  Comparator comparator_7 (.a(InpKeyall), .b(8'h32), .eq(comparator_7_eq));  // open: gt, lt
  Comparator comparator_8 (.a(InpKeyall), .b(8'h33), .eq(comparator_8_eq));  // open: gt, lt
  Comparator comparator_9 (.a(InpKeyall), .b(8'h34), .eq(comparator_9_eq));  // open: gt, lt
  Comparator comparator_10 (.a(InpKeyall), .b(8'h35), .eq(comparator_10_eq));  // open: gt, lt
  Adder #(.width(1)) adder_1 (.a(register_6_q), .b(1'b1), .out(adder_1_out));  // open: cin, cout
  Register #(.width(1)) register_6 (.D(adder_1_out), .Q(register_6_q), .clk(and_1_out), .clr(ATCnewENclc));  // open: en
  and and_1 (and_1_out, ATCinit, mainClk);
  quick quick_1 (.IN(ATCenMove), .OUT(quick_1_out));
  Random #(.width(1)) random_1 (.clk(quick_1_out), .out(random_1_out));  // open: next, clr
  Subtractor subtractor_1 (.a(ATCInpKey), .b(8'h31), .out(subtractor_1_out));  // open: bin, bout
  Comparator #(.mode("unsigned")) comparator_11 (
    .a(playerHPCUR), .b(8'h32), .gt(comparator_11_gt), .eq(comparator_11_eq), .lt(comparator_11_lt));
  or or_6 (or_6_out, comparator_11_eq, comparator_11_lt);
  Comparator #(.mode("unsigned")) comparator_12 (
    .a(playerHPCUR), .b({8{1'b0}}), .eq(comparator_12_eq), .lt(comparator_12_lt));  // open: gt
  and and_2 (InpFlmove31, comparator_1_eq, InpFlpre, ITEMinCELL);
  quick quick_2 (.IN(InpFlmove31), .OUT(INV1ch));
  and and_3 (InpFlmove32, comparator_2_eq, InpFlpre, ITEMinCELL);
  quick quick_3 (.IN(InpFlmove32), .OUT(INV2ch));
  and and_4 (InpFlmove33, comparator_3_eq, InpFlpre, ITEMinCELL);
  quick quick_4 (.IN(InpFlmove33), .OUT(INV3ch));
  and and_5 (InpFlmove34, comparator_4_eq, InpFlpre, ITEMinCELL);
  quick quick_5 (.IN(InpFlmove34), .OUT(INV4ch));
  quick quick_6 (.IN(InpFlmove35), .OUT(INV5ch));
  and and_6 (InpFlmove35, comparator_5_eq, InpFlpre, ITEMinCELL);
  Subtractor subtractor_2 (.a(InpKeyall), .b(8'h31), .out(subtractor_2_out));  // open: bin, bout
  Bit_Extender #(.out_width(3)) bit_extender_1 (.in(subtractor_2_out), .out(bit_extender_1_out));
  assign ATCinit = not_1_out ? not_1_out : 1'bz;  // Controlled_Buffer controlled_buffer_1
  Pull_Resistor pull_resistor_1 (.node(ATCinit));
  Comparator #(.width(1)) comparator_13 (.a(register_6_q), .b(1'b1), .eq(comparator_13_eq));  // open: gt, lt
  not not_1 (not_1_out, comparator_13_eq);
  enemies enemies_1 (
    .ADDR(ATCcurEN), .ELEMIm(ENIMN), .ELEMNm(ENIMN), .Img(ENimgChrst), .Txt(ENNmChrst), .HP(enemies_1_hp),
    .DMG(ENDMGst));
  assign bit_extender_2_out = {{7{1'b0}}, random_1_out};  // Bit_Extender bit_extender_2
  Adder adder_2 (.a(bit_extender_2_out), .b(ENDMG), .out(adder_2_out));  // open: cin, cout
  quick quick_7 (.IN(ATCinisW), .OUT(quick_7_out));
  Multiplexer #(.select(3), .width(8), .enable("false")) multiplexer_1 (
    .in0(INVENTORY1p), .in1(INVENTORY2p), .in2(INVENTORY3p), .in3(INVENTORY4p), .in4(INVENTORY5p),
    .out(multiplexer_1_out), .sel(bit_extender_3_out));  // open: in5, in6, in7
  Bit_Extender #(.out_width(3)) bit_extender_3 (.in(subtractor_1_out), .out(bit_extender_3_out));
  or or_7 (or_7_out, ATCenMoved, ATCuncorrectInp);
  and and_7 (and_7_out, or_7_out, or_8_out);
  // AND_Gate and_8 has open pins: in0=and_7_out, in1=gS2, out=open
  or or_8 (or_8_out, comparator_11_gt, comparator_12_eq);
  and and_9 (InpFl2, or_6_out, not_2_out);
  not not_2 (not_2_out, not_3_out);
  not not_3 (not_3_out, ATCenMoved);
  Comparator comparator_14 (.a(INVENTORY1p), .b(8'h65), .lt(comparator_14_lt));  // open: gt, eq
  and and_10 (and_10_out, comparator_14_lt, comparator_6_eq, comparator_15_gt);
  Comparator comparator_15 (.a(INVENTORY1p), .b(8'h60), .gt(comparator_15_gt));  // open: eq, lt
  Comparator comparator_16 (.a(INVENTORY2p), .b(8'h65), .lt(comparator_16_lt));  // open: gt, eq
  and and_11 (and_11_out, comparator_16_lt, comparator_7_eq, comparator_17_gt);
  Comparator comparator_17 (.a(INVENTORY2p), .b(8'h60), .gt(comparator_17_gt));  // open: eq, lt
  Comparator comparator_18 (.a(INVENTORY3p), .b(8'h65), .lt(comparator_18_lt));  // open: gt, eq
  and and_12 (and_12_out, comparator_18_lt, comparator_8_eq, comparator_19_gt);
  Comparator comparator_19 (.a(INVENTORY3p), .b(8'h60), .gt(comparator_19_gt));  // open: eq, lt
  Comparator comparator_20 (.a(INVENTORY4p), .b(8'h65), .lt(comparator_20_lt));  // open: gt, eq
  and and_13 (and_13_out, comparator_20_lt, comparator_9_eq, comparator_21_gt);
  Comparator comparator_21 (.a(INVENTORY4p), .b(8'h60), .gt(comparator_21_gt));  // open: eq, lt
  Comparator comparator_22 (.a(INVENTORY5p), .b(8'h65), .lt(comparator_22_lt));  // open: gt, eq
  and and_14 (and_14_out, comparator_22_lt, comparator_10_eq, comparator_23_gt);
  Comparator comparator_23 (.a(INVENTORY5p), .b(8'h60), .gt(comparator_23_gt));  // open: eq, lt
  Multiplexer #(.select(3), .width(8), .enable("false")) multiplexer_2 (
    .in0(INVENTORY1p), .in1(INVENTORY2p), .in2(INVENTORY3p), .in3(INVENTORY4p), .in4(INVENTORY5p),
    .out(multiplexer_2_out), .sel(bit_extender_1_out));  // open: in5, in6, in7
  food food_1 (.FOOD(multiplexer_2_out), .GIVEHP(food_1_givehp));
  assign ENHPst = not_1_out ? enemies_1_hp : 8'bz;  // Controlled_Buffer controlled_buffer_2
  Subtractor subtractor_3 (.a(playerHPCUR), .b(adder_2_out), .out(subtractor_3_out));  // open: bin, bout
  Register #(.width(1)) register_7 (
    .D(not_4_out), .Q(register_7_q), .clk(or_9_out), .clr(pull_resistor_7_node));  // open: en
  or or_9 (or_9_out, ATCenMove, quick_8_out);
  quick quick_8 (.IN(ATCinit), .OUT(quick_8_out));
  Pull_Resistor pull_resistor_2 (.node(pull_resistor_2_node));
  weapon weapon_1 (.WEAPON(multiplexer_1_out), .DMG(weapon_1_dmg), .GenRnd(quick_7_out));
  Pull_Resistor pull_resistor_3 (.node(pull_resistor_3_node));
  Comparator #(.mode("unsigned")) comparator_24 (
    .a(weapon_1_dmg), .b(LENHP), .gt(pull_resistor_2_node), .eq(pull_resistor_3_node), .lt(comparator_24_lt));
  Pull_Resistor pull_resistor_4 (.node(comparator_24_lt));
  quick quick_9 (.IN(and_10_out), .OUT(itemRES1));
  quick quick_10 (.IN(and_11_out), .OUT(itemRES2));
  quick quick_11 (.IN(and_12_out), .OUT(itemRES3));
  or or_10 (CHHPinmove, and_10_out, and_11_out, and_12_out, and_13_out, and_14_out);
  quick quick_12 (.IN(and_13_out), .OUT(itemRES4));
  quick quick_13 (.IN(and_14_out), .OUT(itemRES5));
  Adder adder_3 (.a(food_1_givehp), .b(playerHPCUR), .out(adder_3_out));  // open: cin, cout
  Pull_Resistor pull_resistor_5 (.node(pull_resistor_5_node));
  Comparator comparator_25 (.a(adder_3_out), .b(8'h32), .eq(pull_resistor_5_node));  // open: gt, lt
  assign NewPlayerHP = register_7_q ? subtractor_3_out : 8'bz;  // Controlled_Buffer controlled_buffer_3
  assign PLAYERHPCH = register_7_q ? 1'b1 : 1'bz;  // Controlled_Buffer controlled_buffer_4
  buf buffer_1 (ATCenMoved, PLAYERHPCH);
  Pull_Resistor pull_resistor_6 (.node(ATCenMoved));
  not not_4 (not_4_out, register_7_q);
  Pull_Resistor pull_resistor_7 (.node(pull_resistor_7_node));
  buf buffer_2 (pull_resistor_7_node, PLAYERHPCH);
  or or_11 (or_11_out, pull_resistor_2_node, pull_resistor_3_node);
  and and_15 (and_15_out, ATCinisW, comparator_24_lt);
  Subtractor subtractor_4 (.a(ENHP), .b(weapon_1_dmg), .out(subtractor_4_out));  // open: bin, bout
  assign ENHPst = and_18_out ? subtractor_4_out : 8'bz;  // Controlled_Buffer controlled_buffer_5
  Register register_8 (.D(INVENTORY1), .Q(INVENTORY1p), .clk(invchn));  // open: en, clr
  Register register_9 (.D(INVENTORY2), .Q(INVENTORY2p), .clk(invchn));  // open: en, clr
  Register register_10 (.D(INVENTORY3), .Q(INVENTORY3p), .clk(invchn));  // open: en, clr
  Register register_11 (.D(INVENTORY4), .Q(INVENTORY4p), .clk(invchn));  // open: en, clr
  Register register_12 (.D(INVENTORY5), .Q(INVENTORY5p), .clk(invchn));  // open: en, clr
  assign NewPlayerHP = and_16_out ? multiplexer_3_out : 8'bz;  // Controlled_Buffer controlled_buffer_6
  Multiplexer #(.width(8), .enable("false")) multiplexer_3 (
    .in0(adder_3_out), .in1(8'h32), .out(multiplexer_3_out), .sel(pull_resistor_5_node));
  assign PLAYERHPCH = and_16_out ? 1'b1 : 1'bz;  // Controlled_Buffer controlled_buffer_7
  and and_16 (and_16_out, or_12_out, CHHPinmove);
  or or_12 (or_12_out, InpFlpre, ATCInpFlpre);
  and and_17 (and_17_out, ATCInpFlpre, ~ATCuncorrectInp, ATCinisW, or_11_out);  // AND_Gate
  quick quick_14 (.IN(and_18_out), .OUT(ATCnEhp));
  and and_18 (and_18_out, and_15_out, ATCInpFlpre);
  assign MAP_tospace_ELEM = mapPREst1 ? p_x_y__elemOnMap : 12'bz;  // Controlled_Buffer controlled_buffer_8
  quick quick_15 (.IN(mapPREst1), .OUT(stMapCLC1));
  or or_13 (mapPREst1, InpFlmove31, InpFlmove32, InpFlmove33, InpFlmove34, InpFlmove35);
  Comparator comparator_26 (.a(p_x_y), .b(8'h65), .lt(comparator_26_lt));  // open: gt, eq
  and and_19 (and_19_out, comparator_26_lt, comparator_27_gt);
  Comparator comparator_27 (.a(p_x_y), .b(8'h60), .gt(comparator_27_gt));  // open: eq, lt
  Comparator comparator_28 (.a(p_x_y), .b(8'h6b), .lt(comparator_28_lt));  // open: gt, eq
  and and_20 (and_20_out, comparator_28_lt, comparator_29_gt);
  Comparator comparator_29 (.a(p_x_y), .b(8'h65), .gt(comparator_29_gt));  // open: eq, lt
  assign StateCh = and_17_out ? and_17_out : 1'bz;  // Controlled_Buffer controlled_buffer_9
  or or_14 (ITEMinCELL, and_19_out, and_20_out);
  or or_15 (invchn, InpFlpreAtc, \InpFlpreС );
  Comparator #(.width(2)) comparator_30 (.a(PlDir), .b(2'b00), .eq(comparator_30_eq));  // open: gt, lt
  Comparator #(.width(2)) comparator_31 (.a(PlDir), .b(2'b10), .eq(comparator_31_eq));  // open: gt, lt
  Comparator #(.width(2)) comparator_32 (.a(PlDir), .b(2'b01), .eq(comparator_32_eq));  // open: gt, lt
  Comparator #(.width(2)) comparator_33 (.a(PlDir), .b(2'b11), .eq(comparator_33_eq));  // open: gt, lt
  Comparator comparator_34 (.a(ATCInpKey), .b(8'h31), .eq(comparator_34_eq));  // open: gt, lt
  Comparator comparator_35 (.a(ATCInpKey), .b(8'h32), .eq(comparator_35_eq));  // open: gt, lt
  Comparator comparator_36 (.a(ATCInpKey), .b(8'h33), .eq(comparator_36_eq));  // open: gt, lt
  Comparator comparator_37 (.a(ATCInpKey), .b(8'h34), .eq(comparator_37_eq));  // open: gt, lt
  Comparator comparator_38 (.a(ATCInpKey), .b(8'h35), .eq(comparator_38_eq));  // open: gt, lt
  Adder #(.width(4)) adder_4 (.a(4'b0001), .b(register_13_q), .out(adder_4_out));  // open: cin, cout
  Comparator #(.width(4)) comparator_39 (
    .a(4'b1100), .b(register_13_q), .gt(comparator_39_gt), .eq(comparator_39_eq), .lt(comparator_39_lt));
  Register #(.width(4)) register_13 (.D(adder_4_out), .Q(register_13_q), .clk(and_21_out), .clr(invchn));  // open: en
  and and_21 (and_21_out, or_18_out, mainClk);
  Comparator #(.width(4)) comparator_40 (.a(register_13_q), .b(4'b0010), .eq(comparator_40_eq));  // open: gt, lt
  Comparator #(.width(4)) comparator_41 (.a(register_13_q), .b(4'b0011), .eq(comparator_41_eq));  // open: gt, lt
  Comparator #(.width(4)) comparator_42 (.a(register_13_q), .b(4'b0011), .eq(comparator_42_eq));  // open: gt, lt
  Comparator #(.width(4)) comparator_43 (.a(register_13_q), .b(4'b0100), .eq(comparator_43_eq));  // open: gt, lt
  Comparator #(.width(4)) comparator_44 (.a(register_13_q), .b(4'b0100), .eq(comparator_44_eq));  // open: gt, lt
  Comparator #(.width(4)) comparator_45 (.a(register_13_q), .b(4'b0101), .eq(comparator_45_eq));  // open: gt, lt
  Comparator #(.width(4)) comparator_46 (.a(register_13_q), .b(4'b0101), .eq(comparator_46_eq));  // open: gt, lt
  Comparator #(.width(4)) comparator_47 (.a(register_13_q), .b(4'b0110), .eq(comparator_47_eq));  // open: gt, lt
  Comparator #(.width(4)) comparator_48 (.a(register_13_q), .b(4'b0110), .eq(comparator_48_eq));  // open: gt, lt
  Comparator #(.width(4)) comparator_49 (.a(register_13_q), .b(4'b0111), .eq(comparator_49_eq));  // open: gt, lt
  Comparator #(.width(4)) comparator_50 (.a(register_13_q), .b(4'b0111), .eq(comparator_50_eq));  // open: gt, lt
  Comparator #(.width(4)) comparator_51 (.a(register_13_q), .b(4'b1000), .eq(comparator_51_eq));  // open: gt, lt
  Comparator #(.width(4)) comparator_52 (.a(register_13_q), .b(4'b1000), .eq(comparator_52_eq));  // open: gt, lt
  Comparator #(.width(4)) comparator_53 (.a(register_13_q), .b(4'b1001), .eq(comparator_53_eq));  // open: gt, lt
  Comparator #(.width(4)) comparator_54 (.a(register_13_q), .b(4'b1001), .eq(comparator_54_eq));  // open: gt, lt
  Comparator #(.width(4)) comparator_55 (.a(register_13_q), .b(4'b1010), .eq(comparator_55_eq));  // open: gt, lt
  Comparator #(.width(4)) comparator_56 (.a(register_13_q), .b(4'b1010), .eq(comparator_56_eq));  // open: gt, lt
  Comparator #(.width(4)) comparator_57 (.a(register_13_q), .b(4'b1011), .eq(comparator_57_eq));  // open: gt, lt
  not not_5 (not_5_out, comparator_58_eq);
  Comparator comparator_58 (.a(p_x_y_1_t), .b(8'h23), .eq(comparator_58_eq));  // open: gt, lt
  not not_6 (not_6_out, comparator_59_eq);
  Comparator comparator_59 (.a(p_x_y_1), .b(8'h23), .eq(comparator_59_eq));  // open: gt, lt
  not not_7 (not_7_out, comparator_60_eq);
  Comparator comparator_60 (.a(p_x_1_y), .b(8'h23), .eq(comparator_60_eq));  // open: gt, lt
  not not_8 (not_8_out, comparator_61_eq);
  Comparator comparator_61 (.a(p_x_1_y_t), .b(8'h23), .eq(comparator_61_eq));  // open: gt, lt
  Register register_14 (.D(NewMapLevelCh), .Q(mapLevelCur), .clk(MapLevelCh), .clr(mainRES));  // open: en
  Register register_15 (.D(NewPlayerHP), .Q(playerHPCUR), .clk(pull_resistor_8_node), .clr(mainRES));  // open: en
  Pull_Resistor pull_resistor_8 (.node(pull_resistor_8_node));
  buf buffer_3 (pull_resistor_8_node, PLAYERHPCH);
  Register #(.width(2)) register_16 (.D(ATCnewEN), .Q(ATCcurEN), .clk(ATCnewENclc));  // open: en, clr
  Register register_17 (.D(ENHP), .Q(LENHP), .clk(or_16_out));  // open: en, clr
  or or_16 (or_16_out, quick_16_out, quick_17_out);
  quick quick_16 (.IN(ATCinisW), .OUT(quick_16_out));
  quick quick_17 (.IN(ATCinit), .OUT(quick_17_out));
  quick quick_18 (.IN(demultiplexer_1_out1), .OUT(\InpFlpreС ));
  or or_17 (letsPrint, memReadyToPrint, gS0);
  or or_18 (or_18_out, comparator_39_gt, comparator_39_lt);
  and and_22 (and_22_out, not_5_out, WonInp, comparator_30_eq);
  and and_23 (and_23_out, not_6_out, WonInp, comparator_31_eq);
  and and_24 (and_24_out, not_7_out, WonInp, comparator_32_eq);
  and and_25 (and_25_out, not_8_out, WonInp, comparator_33_eq);
  Comparator comparator_62 (.a(INVENTORY1p), .b(8'h6b), .lt(comparator_62_lt));  // open: gt, eq
  and and_26 (and_26_out, comparator_62_lt, comparator_34_eq, comparator_63_gt);
  Comparator comparator_63 (.a(INVENTORY1p), .b(8'h65), .gt(comparator_63_gt));  // open: eq, lt
  Comparator comparator_64 (.a(INVENTORY2p), .b(8'h6b), .lt(comparator_64_lt));  // open: gt, eq
  and and_27 (and_27_out, comparator_64_lt, comparator_35_eq, comparator_65_gt);
  Comparator comparator_65 (.a(INVENTORY2p), .b(8'h65), .gt(comparator_65_gt));  // open: eq, lt
  Comparator comparator_66 (.a(INVENTORY3p), .b(8'h6b), .lt(comparator_66_lt));  // open: gt, eq
  and and_28 (and_28_out, comparator_66_lt, comparator_36_eq, comparator_67_gt);
  Comparator comparator_67 (.a(INVENTORY3p), .b(8'h65), .gt(comparator_67_gt));  // open: eq, lt
  Comparator comparator_68 (.a(INVENTORY4p), .b(8'h6b), .lt(comparator_68_lt));  // open: gt, eq
  and and_29 (and_29_out, comparator_68_lt, comparator_37_eq, comparator_69_gt);
  Comparator comparator_69 (.a(INVENTORY4p), .b(8'h65), .gt(comparator_69_gt));  // open: eq, lt
  Comparator comparator_70 (.a(INVENTORY5p), .b(8'h6b), .lt(comparator_70_lt));  // open: gt, eq
  and and_30 (and_30_out, comparator_70_lt, comparator_38_eq, comparator_71_gt);
  Comparator comparator_71 (.a(INVENTORY5p), .b(8'h65), .gt(comparator_71_gt));  // open: eq, lt
  Demultiplexer #(.select(2), .disabled(0), .enable("false")) demultiplexer_1 (
    .out0(InpFlpreSTRT), .out1(demultiplexer_1_out1), .out2(ATCInpFlpre), .in(CONSOLE_PRINTER_it_worked),
    .sel(gameState));  // open: out3
  Demultiplexer #(.select(2), .width(8), .disabled(0), .enable("false")) demultiplexer_2 (
    .out1(InpKey), .out2(ATCInpKey), .in(InpKeyall), .sel(gameState));  // open: out0, out3
  consoler CONSOLE_PRINTER (
    .CLK(mainClk), .RESET(letsPrint), .IT_WORKED(CONSOLE_PRINTER_it_worked), .INPUT_CHAR(InpKeyall),
    .PRINT_SIZE(tpLen), .MEM_A(memN), .MEM_D(memChar), .CONNECTED(CONSOLE_PRINTER_connected));  // open: INPUT_were
  Lquick lquick_1 (.IN(comparator_39_eq), .OUT(InpFlpre), .CLC(mainClk));
  assign MAP_tospace_ELEM = comparator_40_eq ? p_x_y__elemOnMap : 12'bz;  // Controlled_Buffer controlled_buffer_10
  assign MAP_tospace_ELEM = comparator_42_eq ? p_x_y_1__elemOnMap_t : 12'bz;  // Controlled_Buffer controlled_buffer_11
  assign MAP_tospace_ELEM = comparator_44_eq ? p_x_y_1__elemOnMap : 12'bz;  // Controlled_Buffer controlled_buffer_12
  assign MAP_tospace_ELEM = comparator_46_eq ? p_x_1_y__elemOnMap_t : 12'bz;  // Controlled_Buffer controlled_buffer_13
  assign MAP_tospace_ELEM = comparator_48_eq ? p_x_1_y__elemOnMap : 12'bz;  // Controlled_Buffer controlled_buffer_14
  assign MAP_tospace_ELEM = comparator_50_eq ? p_x_2_y__elemOnMap : 12'bz;  // Controlled_Buffer controlled_buffer_15
  assign MAP_tospace_ELEM = comparator_52_eq ? p_x_2_y__elemOnMap_t : 12'bz;  // Controlled_Buffer controlled_buffer_16
  assign MAP_tospace_ELEM = comparator_54_eq ? p_x_y_2__elemOnMap_t : 12'bz;  // Controlled_Buffer controlled_buffer_17
  assign MAP_tospace_ELEM = comparator_56_eq ? p_x_y_2__elemOnMap : 12'bz;  // Controlled_Buffer controlled_buffer_18
  Subtractor subtractor_5 (.a(PLyOM), .b(8'h1), .out(subtractor_5_out));  // open: bin, bout
  assign NewPLyOM = and_22_out ? subtractor_5_out : 8'bz;  // Controlled_Buffer controlled_buffer_19
  assign NewPLyOM = and_23_out ? adder_5_out : 8'bz;  // Controlled_Buffer controlled_buffer_20
  Adder adder_5 (.a(PLyOM), .b(8'h1), .out(adder_5_out));  // open: cin, cout
  assign NewPLxOM = and_24_out ? adder_6_out : 8'bz;  // Controlled_Buffer controlled_buffer_21
  Adder adder_6 (.a(PLxOM), .b(8'h1), .out(adder_6_out));  // open: cin, cout
  Subtractor subtractor_6 (.a(PLxOM), .b(8'h1), .out(subtractor_6_out));  // open: bin, bout
  assign NewPLxOM = and_25_out ? subtractor_6_out : 8'bz;  // Controlled_Buffer controlled_buffer_22
  and and_31 (ATCinisW, ATCInpFlpre, or_19_out);
  or or_19 (or_19_out, and_26_out, and_27_out, and_28_out, and_29_out, and_30_out);
  not not_9 (not_9_out, ATCinisW);
  buf buffer_4 (buffer_4_out, StateCh);
  Pull_Resistor pull_resistor_9 (.node(buffer_4_out));
  Register register_18 (.D(ENDMGst), .Q(ENDMG), .clk(ATCinit));  // open: en, clr
  Register register_19 (.D(ENHPst), .Q(ENHP), .clk(or_20_out));  // open: en, clr
  or or_20 (or_20_out, ATCnEhp, ATCinit);
  LED connected (.in(CONSOLE_PRINTER_connected));
  LED data_was ();  // open: in
  Register register_20 (.D(objectONmap), .Q(p_x_y), .clk(comparator_41_eq));  // open: en, clr
  Register register_21 (.D(objectONmap), .Q(p_x_y_1_t), .clk(comparator_43_eq));  // open: en, clr
  Register register_22 (.D(objectONmap), .Q(p_x_y_1), .clk(comparator_45_eq));  // open: en, clr
  Register register_23 (.D(objectONmap), .Q(p_x_1_y_t), .clk(comparator_47_eq));  // open: en, clr
  Register register_24 (.D(objectONmap), .Q(p_x_1_y), .clk(comparator_49_eq));  // open: en, clr
  Register register_25 (.D(objectONmap), .Q(p_x_2_y), .clk(comparator_51_eq));  // open: en, clr
  Register register_26 (.D(objectONmap), .Q(p_x_2_y_t), .clk(comparator_53_eq));  // open: en, clr
  Register register_27 (.D(objectONmap), .Q(p_x_y_2), .clk(comparator_55_eq));  // open: en, clr
  Register register_28 (.D(objectONmap), .Q(p__y_2), .clk(comparator_57_eq));  // open: en, clr
  and and_32 (ATCuncorrectInp, not_9_out, ATCInpFlpre);
  Register #(.width(2)) register_29 (.D(gSto), .Q(gameState), .clk(buffer_4_out), .clr(mainRES));  // open: en
  Register #(.width(2)) register_30 (.D(NewPlDir), .Q(PlDir), .clk(PlDirCh), .clr(mainRES));  // open: en
  quick quick_19 (.IN(or_21_out), .OUT(changePCy));
  or or_21 (or_21_out, and_22_out, and_23_out);
  or or_22 (InpFlmove2, or_21_out, or_23_out);
  or or_23 (or_23_out, and_24_out, and_25_out);
  quick quick_20 (.IN(or_23_out), .OUT(changePCx));
  and and_33 (and_33_out, ATCuncorrectInp, gS2);
  quick quick_21 (.IN(or_24_out), .OUT(ATCenMove));
  or or_24 (or_24_out, and_33_out, ATCinisW);
  and and_34 (and_34_out, InpFl1, gS1);
  or or_25 (or_25_out, and_34_out, and_35_out);
  and and_35 (and_35_out, InpFl2, gS2);
  x_y__to_memory_elem_number x_y_____elem (.H(MapW), .Y(PLyOM), .X(PLxOM), .ELEM(p_x_y__elemOnMap), .START(12'h4));
  x_y__to_memory_elem_number x_y_____elem_2 (
    .H(MapW), .Y(adder_7_out), .X(PLxOM), .ELEM(p_x_y_1__elemOnMap), .START(12'h4));
  Adder adder_7 (.a(PLyOM), .b(8'h1), .out(adder_7_out));  // open: cin, cout
  x_y__to_memory_elem_number x_y_____elem_3 (
    .H(MapW), .Y(PLyOM), .X(adder_8_out), .ELEM(p_x_1_y__elemOnMap), .START(12'h4));
  Adder adder_8 (.a(PLxOM), .b(8'h1), .out(adder_8_out));  // open: cin, cout
  Adder #(.width(3)) adder_9 (.a(3'b001), .b(register_31_q), .out(adder_9_out));  // open: cin, cout
  Comparator #(.width(3)) comparator_72 (
    .a(3'b111), .b(register_31_q), .gt(InpFl1), .lt(comparator_72_lt));  // open: eq
  Register #(.width(3)) register_31 (
    .D(adder_9_out), .Q(register_31_q), .clk(and_36_out), .clr(TOPRINTRES));  // open: en
  and and_36 (and_36_out, comparator_72_lt, mainClk);
  quick quick_22 (.IN(InpFlpre), .OUT(TOPRINTRES));
  Comparator #(.width(2)) comparator_73 (.a(PlDir), .b(2'b00), .eq(comparator_73_eq));  // open: gt, lt
  Comparator #(.width(2)) comparator_74 (.a(PlDir), .b(2'b10), .eq(comparator_74_eq));  // open: gt, lt
  Comparator #(.width(2)) comparator_75 (.a(PlDir), .b(2'b01), .eq(comparator_75_eq));  // open: gt, lt
  Comparator #(.width(2)) comparator_76 (.a(PlDir), .b(2'b11), .eq(comparator_76_eq));  // open: gt, lt
  Multiplexer #(.width(8), .enable("false")) multiplexer_4 (
    .in0(8'h20), .in1(mapSTDATAreaded), .out(multiplexer_4_out), .sel(not_10_out));
  graphic_elems graphic_elems_1 (.ADDR(gStdtScrMem), .ELEM(memN), .DATA(memChar), .LEN(tpLen));
  LED led_1 (.in(memReadyToPrint));
  or or_26 (memReadyToPrint, button_1_out, quick_23_out);
  Button button_1 (.out(button_1_out));
  quick quick_23 (.IN(or_25_out), .OUT(quick_23_out));
  Comparator comparator_77 (.a(p_x_y_1_t), .b(8'h30), .gt(comparator_77_gt));  // open: eq, lt
  Comparator comparator_78 (.a(p_x_y_1), .b(8'h30), .gt(comparator_78_gt));  // open: eq, lt
  Comparator comparator_79 (.a(p_x_1_y), .b(8'h30), .gt(comparator_79_gt));  // open: eq, lt
  Comparator comparator_80 (.a(p_x_1_y_t), .b(8'h30), .gt(comparator_80_gt));  // open: eq, lt
  Multiplexer #(.width(12), .enable("false")) multiplexer_5 (
    .in0(MAP_tospace_ELEM), .in1(mapSTelemREAD), .out(multiplexer_5_out), .sel(not_10_out));
  Subtractor subtractor_7 (.a(PLyOM), .b(8'h1), .out(subtractor_7_out));  // open: bin, bout
  Subtractor subtractor_8 (.a(PLxOM), .b(8'h1), .out(subtractor_8_out));  // open: bin, bout
  Adder adder_10 (.a(PLxOM), .b(8'h2), .out(adder_10_out));  // open: cin, cout
  Comparator comparator_81 (.a(p_x_y_1_t), .b(8'h35), .lt(comparator_81_lt));  // open: gt, eq
  Comparator comparator_82 (.a(p_x_y_1), .b(8'h35), .lt(comparator_82_lt));  // open: gt, eq
  Comparator comparator_83 (.a(p_x_1_y), .b(8'h35), .lt(comparator_83_lt));  // open: gt, eq
  Comparator comparator_84 (.a(p_x_1_y_t), .b(8'h35), .lt(comparator_84_lt));  // open: gt, eq
  Register #(.width(12)) register_32 (
    .D(adder_11_out), .Q(mapSTelemREAD), .clk(and_37_out), .clr(mainRES));  // open: en
  and and_37 (and_37_out, not_10_out, mainClk);
  x_y__to_memory_elem_number x_y_____elem_4 (
    .H(MapW), .Y(subtractor_7_out), .X(PLxOM), .ELEM(p_x_y_1__elemOnMap_t), .START(12'h4));
  x_y__to_memory_elem_number x_y_____elem_5 (
    .H(MapW), .Y(PLyOM), .X(subtractor_8_out), .ELEM(p_x_1_y__elemOnMap_t), .START(12'h4));
  x_y__to_memory_elem_number x_y_____elem_6 (
    .H(MapW), .Y(PLyOM), .X(adder_10_out), .ELEM(p_x_2_y__elemOnMap), .START(12'h4));
  // Probe on InpKey
  Subtractor subtractor_9 (.a(p_x_y_1_t), .b(8'h31), .out(subtractor_9_out));  // open: bin, bout
  Subtractor subtractor_10 (.a(p_x_1_y_t), .b(8'h31), .out(subtractor_10_out));  // open: bin, bout
  Adder #(.width(12)) adder_11 (.a(mapSTelemREAD), .b(12'h1), .out(adder_11_out));  // open: cin, cout
  assign MAP_tospace_ELEM = and_38_out ? p_x_y_1__elemOnMap_t : 12'bz;  // Controlled_Buffer controlled_buffer_23
  assign ATCnewEN = and_38_out ? bit_extender_4_out : 2'bz;  // Controlled_Buffer controlled_buffer_24
  Bit_Extender #(.out_width(2)) bit_extender_4 (.in(subtractor_9_out), .out(bit_extender_4_out));
  and and_38 (and_38_out, comparator_77_gt, comparator_81_lt, comparator_73_eq);
  and and_39 (and_39_out, comparator_78_gt, comparator_82_lt, comparator_74_eq);
  and and_40 (and_40_out, comparator_79_gt, comparator_83_lt, comparator_75_eq);
  and and_41 (and_41_out, comparator_80_gt, comparator_84_lt, comparator_76_eq);
  assign ATCnewEN = and_41_out ? bit_extender_5_out : 2'bz;  // Controlled_Buffer controlled_buffer_25
  Bit_Extender #(.out_width(2)) bit_extender_5 (.in(subtractor_10_out), .out(bit_extender_5_out));
  assign MAP_tospace_ELEM = and_41_out ? p_x_1_y__elemOnMap_t : 12'bz;  // Controlled_Buffer controlled_buffer_26
  RAM #(.addrWidth(12), .bus("separate")) ram_1 (
    .addr(multiplexer_5_out), .din(multiplexer_4_out), .data(objectONmap), .str(mapPREst), .clk(stMapCLC));  // open: sel, ld, clr
  Comparator #(.width(12)) comparator_85 (.a(mapSTelemREAD), .b(12'h94), .eq(comparator_85_eq));  // open: gt, lt
  not not_10 (not_10_out, comparator_85_eq);
  or or_27 (mapPREst, not_10_out, ATCnewENclc, mapPREst1);
  or or_28 (stMapCLC, and_37_out, stMapCLC2, stMapCLC1);
  Comparator comparator_86 (.a(InpKey), .b(8'h61), .eq(comparator_86_eq));  // open: gt, lt
  not not_11 (not_11_out, InpFlmove1);
  or or_29 (InpFlmove1, comparator_86_eq, comparator_87_eq);
  Comparator comparator_87 (.a(InpKey), .b(8'h64), .eq(comparator_87_eq));  // open: gt, lt
  Comparator comparator_88 (.a(InpKey), .b(8'h77), .eq(WonInp));  // open: gt, lt
  quick quick_24 (.IN(comparator_89_eq), .OUT(qres));
  Comparator comparator_89 (.a(InpKey), .b(8'h71), .eq(comparator_89_eq));  // open: gt, lt
  Subtractor subtractor_11 (.a(p_x_y_1), .b(8'h31), .out(subtractor_11_out));  // open: bin, bout
  not not_12 (not_12_out, not_13_out);
  not not_13 (not_13_out, ATCnewENclc);
  not not_14 (not_14_out, not_12_out);
  or or_30 (ATCnewENclc, and_38_out, and_39_out, and_40_out, and_41_out);
  assign StateCh = ATCnewENclc ? ATCnewENclc : 1'bz;  // Controlled_Buffer controlled_buffer_27
  Subtractor subtractor_12 (.a(p_x_1_y), .b(8'h31), .out(subtractor_12_out));  // open: bin, bout
  x_y__to_memory_elem_number x_y_____elem_7 (
    .H(MapW), .Y(subtractor_13_out), .X(PLxOM), .ELEM(p_x_y_2__elemOnMap_t), .START(12'h4));
  Subtractor subtractor_13 (.a(PLyOM), .b(8'h2), .out(subtractor_13_out));  // open: bin, bout
  x_y__to_memory_elem_number x_y_____elem_8 (
    .H(MapW), .Y(PLyOM), .X(subtractor_14_out), .ELEM(p_x_2_y__elemOnMap_t), .START(12'h4));
  Subtractor subtractor_14 (.a(PLxOM), .b(8'h2), .out(subtractor_14_out));  // open: bin, bout
  x_y__to_memory_elem_number x_y_____elem_9 (
    .H(MapW), .Y(adder_12_out), .X(PLyOM), .ELEM(p_x_y_2__elemOnMap), .START(12'h4));
  Adder adder_12 (.a(PLxOM), .b(8'h2), .out(adder_12_out));  // open: cin, cout
  Adder #(.width(2)) adder_13 (.a(PlDir), .b(2'b01), .out(adder_13_out));  // open: cin, cout
  Subtractor #(.width(2)) subtractor_15 (.a(PlDir), .b(2'b01), .out(subtractor_15_out));  // open: bin, bout
  quick quick_25 (.IN(not_15_out), .OUT(PlDirCh));
  not not_15 (not_15_out, not_11_out);
  assign MAP_tospace_ELEM = and_39_out ? p_x_y_1__elemOnMap : 12'bz;  // Controlled_Buffer controlled_buffer_28
  Bit_Extender #(.out_width(2)) bit_extender_6 (.in(subtractor_11_out), .out(bit_extender_6_out));
  assign ATCnewEN = and_39_out ? bit_extender_6_out : 2'bz;  // Controlled_Buffer controlled_buffer_29
  not not_16 (stMapCLC2, not_14_out);
  quick quick_26 (.IN(ATCnewENclc), .OUT(InpFlpreAtc));
  Bit_Extender #(.out_width(2)) bit_extender_7 (.in(subtractor_12_out), .out(bit_extender_7_out));
  assign ATCnewEN = and_40_out ? bit_extender_7_out : 2'bz;  // Controlled_Buffer controlled_buffer_30
  assign MAP_tospace_ELEM = and_40_out ? p_x_1_y__elemOnMap : 12'bz;  // Controlled_Buffer controlled_buffer_31
  Multiplexer #(.width(2), .enable("false")) multiplexer_6 (
    .in0(adder_13_out), .in1(subtractor_15_out), .out(NewPlDir), .sel(comparator_86_eq));
  LED led_2 (.in(demultiplexer_3_out3));
  LED led_3 (.in(demultiplexer_3_out3));
  Button button_2 (.out(button_2_out));
  buf or_31 (or_31_out, qres);  // OR_Gate
  LED led_4 (.in(demultiplexer_3_out0));
  LED led_5 (.in(demultiplexer_3_out0));
  Demultiplexer #(.select(2), .enable("false")) demultiplexer_3 (
    .out0(demultiplexer_3_out0), .out1(demultiplexer_3_out1), .out2(demultiplexer_3_out2),
    .out3(demultiplexer_3_out3), .in(1'b1), .sel(PlDir));
  LED led_6 (.in(demultiplexer_3_out1));
  LED led_7 (.in(demultiplexer_3_out1));
  LED led_8 (.in(demultiplexer_3_out2));
  LED led_9 (.in(demultiplexer_3_out2));
  LED led_10 (.in(demultiplexer_4_out0));
  LED led_11 (.in(demultiplexer_4_out1));
  LED led_12 (.in(demultiplexer_4_out2));
  Multiplexer #(.width(8), .enable("false")) multiplexer_7 (
    .in0(NewPLxOM), .in1(maps_1_xpp), .out(multiplexer_7_out), .sel(gS0));
  Register #(.width(12)) u_mapW (.D(maps_1_width), .Q(MapW), .clk(LoadMap));  // open: en, clr
  Comparator #(.width(2)) comparator_90 (.a(2'b00), .b(gameState), .eq(gS0));  // open: gt, lt
  Comparator #(.width(2)) comparator_91 (.a(2'b01), .b(gameState), .eq(gS1));  // open: gt, lt
  Comparator #(.width(2)) comparator_92 (.a(2'b10), .b(gameState), .eq(gS2));  // open: gt, lt
  and and_42 (mainClk, ~mainRES, clock_1_out);  // AND_Gate
  Clock clock_1 (.out(clock_1_out));
  or or_32 (mainRES, button_2_out, or_31_out);
  // Probe on playerHPCUR
  // Probe on ENHP
  // Probe on ATCcurEN
  Demultiplexer #(.select(2), .enable("false")) demultiplexer_4 (
    .out0(demultiplexer_4_out0), .out1(demultiplexer_4_out1), .out2(demultiplexer_4_out2), .in(1'b1),
    .sel(gameState));  // open: out3
  Register Xpp (.D(multiplexer_7_out), .Q(PLxOM), .clk(or_33_out));  // open: en, clr
  or or_33 (or_33_out, changePCx, LoadMap);
  assign NewPlayerHP = LoadMap ? 8'h32 : 8'bz;  // Controlled_Buffer controlled_buffer_32
  buf buffer_5 (LoadMap, and_43_out);
  and and_43 (and_43_out, InpFlpreSTRT, gS0);
  quick quick_27 (.IN(chGM), .OUT(quick_27_out));
  // Probe on PLxOM
  // Probe on PLyOM
  Multiplexer #(.width(8), .enable("false")) multiplexer_8 (
    .in0(NewPLyOM), .in1(maps_1_ypp), .out(multiplexer_8_out), .sel(gS0));
  or or_34 (or_34_out, changePCy, LoadMap);
  maps maps_1 (
    .ADDR(mapLevelCur), .ELEM(mapSTelemREAD), .DATA(mapSTDATAreaded), .Xpp(maps_1_xpp), .Ypp(maps_1_ypp),
    .Width(maps_1_width), .Height(maps_1_height));  // open: LEN
  Register #(.width(12)) u_mapH (.D(maps_1_height), .Q(MapH), .clk(LoadMap));  // open: en, clr
  assign StateCh = or_35_out ? or_35_out : 1'bz;  // Controlled_Buffer controlled_buffer_33
  or or_35 (or_35_out, and_43_out, quick_27_out);
  Register Ypp (.D(multiplexer_8_out), .Q(PLyOM), .clk(or_34_out));  // open: en, clr
  assign PLAYERHPCH = quick_28_out ? quick_28_out : 1'bz;  // Controlled_Buffer controlled_buffer_34
  quick quick_28 (.IN(or_35_out), .OUT(quick_28_out));
  Multiplexer #(.select(2), .width(2), .enable("false")) multiplexer_9 (
    .in0(2'b01), .in1(2'b10), .in2(2'b01), .out(gSto), .sel({gS2, gS1}));  // open: in3
  Multiplexer #(.select(2), .width(8), .enable("false")) multiplexer_10 (
    .in0(8'h1f), .in1({8{1'b0}}), .in2(8'h1e), .out(gStdtScrMem), .sel({gS2, gS1}));  // open: in3
  assign PLAYERHPCH = 1'b0 ? 1'b0 : 1'bz;  // Controlled_Buffer controlled_buffer_35
  Controlled_Buffer #(.width(8)) controlled_buffer_36 (.out(NewPlayerHP), .en(1'b0));  // open: in

  // Other names for the same wires on the sheet: ATCinit1 = ATCinit; mapPREst2 = ATCnewENclc;
  //   p_x_y_obj[7:0] = objectONmap

  // Notes on the sheet:
  //   INVETORY
  //   BATTLE MODE
  //   inp: 1
  //   inp: 2
  //   inp: 3
  //   inp: 4
  //   inp: 5
  //   CURREBT STATE
  //   inp: 1
  //   inp: 2
  //   inp: 3
  //   inp: 4
  //   inp: 5
  //   enemy won
  //   CONTINUE GAME
  //   is it eat in cell
  //   is it weapon in cell
  //   PREVIOUS STATE
  //   EAT FOOD
  //   ENEMY INIT
  //   ENEMY ATTACK
  //   CHECK PLAYER HAS WON
  //   CHECK PLAYER HAS LOST
  //   REMOVE ITEM FROM GAME MAP
  //   INVENTORY REGISTERS
  //   enemy attaked
  //   player won
  //   PLAYER MOVEMENT
  //   inp: 1
  //   inp: 2
  //   inp: 3
  //   inp: 4
  //   inp: 5
  //   SOME GLOBAL VARIBLES
  //   Curent map level
  //   Player HP
  //   Current Enemy number
  //   Last Enemy hp
  //   3
  //   BATTLE MODE VARIBLES
  //   PRINTING ON SCREEN
  //   GET SOME ADJACENT CELLS
  //   weapon in cell
  //   Game state
  //   0 - start screen 1 - walking 2 - battle
  //   Player Direction
  //   0
  //   ->
  //   1
  //   2
  //   Current Enemy dmg
  //   Current Enemy hp
  //   DO FORWARD STEP
  //   ATTACK THE ENEMY
  //   Player (y+1,x) cell
  //   Player (y,x+1) cell
  //   КОСТЫЛЬ
  //   player do something
  //   GAME MAP
  //   RENDERING OF SCREEN
  //   Player cell
  //   RENDERING COMPLITE
  //   Player (y-1,x) cell
  //   Player (y,x-1) cell
  //   Player (y,x+2) cell
  //   FOR WORK.....
  //   inp: a
  //   inp: d
  //   inp: w
  //   inp: q
  //   GET SOME ADJACENT CELLS COORDINATES
  //   Player (y-2,x) cell
  //   Player (y,x-2) cell
  //   Player (y+2,x) cell
  //   MEET ENEMY AND CHANGE GAME MODE TO BATTLE
  //   PARSE INPUT
  //   MAKE A TURN
  //   START
  //   WALK
  //   BATTLE
  //   pHP
  //   eHP
  //   curENEMY
  //   INITIALIZING GAME MAP
  //   GAME MODE CHANGER
  //   DEBUG TOOLS
  //   GAME INFORAMTION
  //   player direction
  //   pX
  //   pY
  //   reset game
endmodule

// CP
module consoler (
  input  [7:0] MEM_D,
  input  CLK,
  input  [11:0] PRINT_SIZE,
  input  RESET,
  output IT_WORKED,
  output [7:0] INPUT_CHAR,
  output CONNECTED,
  output INPUT_were,
  output [11:0] MEM_A
);

  wire and_3_out, and_4_out, clc, comparator_1_eq, not_1_out, not_2_out, not_3_out, not_4_out, not_5_out,
       not_6_out, or_1_out, PRND, readConsole, register_2_q, RES, RESET_MEMORY_COUNTER_out, uart_1_p3,
       uart_1_p7;
  wire [7:0] uart_1_p1;
  wire [11:0] adder_1_out;

  and and_1 (IT_WORKED, not_3_out, PRND, INPUT_were);
  Register #(.width(1)) register_1 (.D(not_1_out), .Q(INPUT_were), .clk(or_1_out));  // open: en, clr
  not not_1 (not_1_out, INPUT_were);
  or or_1 (or_1_out, RES, uart_1_p3);
  and and_2 (clc, CLK, not_2_out);
  not not_2 (not_2_out, RES);
  not not_3 (not_3_out, uart_1_p3);
  not not_4 (not_4_out, RESET);
  and and_3 (and_3_out, clc, comparator_1_eq);
  Register #(.width(1)) register_2 (.D(RESET), .Q(register_2_q), .clk(RESET), .clr(not_5_out));  // open: en
  not not_5 (not_5_out, not_4_out);
  Register register_3 (.D(uart_1_p1), .Q(INPUT_CHAR), .clk(and_3_out), .clr(RES));  // open: en
  or or_2 (RES, register_2_q, RESET_MEMORY_COUNTER_out);
  Button RESET_MEMORY_COUNTER (.out(RESET_MEMORY_COUNTER_out));
  Comparator comparator_1 (.a(INPUT_CHAR), .b({8{1'b0}}), .eq(comparator_1_eq));  // open: gt, lt
  not not_6 (not_6_out, PRND);
  Register #(.width(12)) register_4 (.D(adder_1_out), .Q(MEM_A), .clk(and_4_out), .clr(RES));  // open: en
  not not_7 (readConsole, PRND);
  and and_4 (and_4_out, not_6_out, clc);
  // UART uart_1: pin names not known; wires that end beside it: uart_1_p1, MEM_D, uart_1_p3, clc, uart_1_p3, CONNECTED, uart_1_p7
  Adder #(.width(12)) adder_1 (.a(MEM_A), .b(12'h1), .out(adder_1_out));  // open: cin, cout
  or or_3 (uart_1_p7, uart_1_p3, readConsole);
  Comparator #(.width(12)) comparator_2 (.a(MEM_A), .b(PRINT_SIZE), .eq(PRND));  // open: gt, lt

  // Notes on the sheet:
  //   12 бит адрес
  //   Frame Printed
  //   Print Frame
  //   A - Адрес к каторому обращается
  //   B - элемент по адресу
endmodule

// GE
module graphic_elems (
  input  [7:0] ADDR,
  input  [11:0] ELEM,
  output [7:0] DATA,
  output [11:0] LEN
);

  wire [7:0] deMux1, geD0, geD1, geD2, geD2_0, geD2_1, geD3, geD4, geD5, geD6, geD7, geD8, geD9, geD10,
       geD11, geD12, geD13, geD14, geD15;
  wire [11:0] deMuxl1;

  ROM #(.addrWidth(12)) rom_1 (.addr(ELEM), .data(geD0));  // open: sel
  ROM #(.addrWidth(12)) rom_2 (.addr(ELEM), .data(geD1));  // open: sel
  ROM #(.addrWidth(12)) rom_3 (.addr(ELEM), .data(geD2));  // open: sel
  ROM #(.addrWidth(12)) rom_4 (.addr(ELEM), .data(geD3));  // open: sel
  ROM #(.addrWidth(12)) rom_5 (.addr(ELEM), .data(geD4));  // open: sel
  ROM #(.addrWidth(12)) rom_6 (.addr(ELEM), .data(geD5));  // open: sel
  ROM #(.addrWidth(12)) rom_7 (.addr(ELEM), .data(geD6));  // open: sel
  ROM #(.addrWidth(12)) rom_8 (.addr(ELEM), .data(geD7));  // open: sel
  ROM #(.addrWidth(12)) rom_9 (.addr(ELEM), .data(geD8));  // open: sel
  ROM #(.addrWidth(12)) rom_10 (.addr(ELEM), .data(geD9));  // open: sel
  ROM #(.addrWidth(12)) rom_11 (.addr(ELEM), .data(geD10));  // open: sel
  ROM #(.addrWidth(12)) rom_12 (.addr(ELEM), .data(geD11));  // open: sel
  ROM #(.addrWidth(12)) rom_13 (.addr(ELEM), .data(geD12));  // open: sel
  ROM #(.addrWidth(12)) rom_14 (.addr(ELEM), .data(geD13));  // open: sel
  ROM #(.addrWidth(12)) rom_15 (.addr(ELEM), .data(geD14));  // open: sel
  ROM #(.addrWidth(12)) rom_16 (.addr(ELEM), .data(geD15));  // open: sel
  ROM #(.addrWidth(12)) rom_17 (.addr(ELEM), .data(geD2_0));  // open: sel
  ROM #(.addrWidth(12)) rom_18 (.addr(ELEM), .data(geD2_1));  // open: sel
  Multiplexer #(.select(5), .width(8), .enable("false")) multiplexer_1 (
    .in0(geD0), .in1(geD1), .in2(geD2), .in3(geD3), .in4(geD4), .in5(geD5), .in6(geD6), .in7(geD7),
    .in8(geD8), .in9(geD9), .in10(geD10), .in11(geD11), .in12(geD12), .in13(geD13), .in14(geD14),
    .in15(geD15), .in30(geD2_1), .in31(geD2_0), .out(deMux1), .sel(ADDR[4:0]));  // open: in16, in17, in18, in19, in20, in21, in22, in23, in24, in25, in26, in27, in28, in29
  Multiplexer #(.select(5), .width(12), .enable("false")) multiplexer_2 (
    .in0(12'had5), .in1(12'h596), .in2(12'h596), .in3(12'h596), .in4(12'h596), .in5(12'h596), .in6(12'h596),
    .in7(12'h596), .in8(12'h596), .in9(12'h596), .in10(12'h596), .in11(12'h596), .in12(12'h596),
    .in13(12'h596), .in14(12'h596), .in15(12'h596), .in30(12'had5), .in31(12'had5), .out(deMuxl1),
    .sel(ADDR[4:0]));  // open: in16, in17, in18, in19, in20, in21, in22, in23, in24, in25, in26, in27, in28, in29
  Multiplexer #(.select(3), .width(8), .enable("false")) multiplexer_3 (
    .in0(deMux1), .out(DATA), .sel(ADDR[7:5]));  // open: in1, in2, in3, in4, in5, in6, in7
  Multiplexer #(.select(3), .width(12), .enable("false")) multiplexer_4 (
    .in0(deMuxl1), .out(LEN), .sel(ADDR[7:5]));  // open: in1, in2, in3, in4, in5, in6, in7

  // Other names for the same wires on the sheet: geAddr1[4:0] = ADDR[4:0]; geAddr2[2:0] = ADDR[7:5];
  //   geEl[11:0] = ELEM

  // Notes on the sheet:
  //   BOARD
  //   contents of rom_1 (hex, n*v repeats v):
  //   0 76*23 a 23 52*20 23 21*20 23 a 23 52*20 23 21*20 23 a 23 52*20 23 21*20 23 a 23 52*20 23 21*20 23
  //   a 23 52*20 23 21*20 23 a 23 52*20 23 21*20 23 a 23 52*20 23 21*20 23 a 23 52*20 23 21*20 23 a 23
  //   52*20 23 21*20 23 a 23 52*20 23 21*20 23 a 23 52*20 23 21*20 23 a 23 52*20 23 21*20 23 a 23 52*20 23
  //   21*20 23 a 23 52*20 23 21*20 23 a 23 52*20 23 21*20 23 a 23 52*20 23 21*20 23 a 23 52*20 23 21*20 23
  //   a 23 52*20 23 21*20 23 a 23 52*20 23 21*20 23 a 23 52*20 23 21*20 23 a 23 52*20 23 21*20 23 a 23
  //   52*20 23*23 a 23 52*20 23 21*20 23 a 23 52*20 23 21*20 23 a 23 52*20 23 21*20 23 a 23 52*20 23 21*20
  //   23 a 23 52*20 23 21*20 23 a 76*23 a 23 74*20 23 a 76*23 a 23 9*20 23 9*20 23 9*20 23 9*20 23 9*20 23
  //   20 48 50 20 7c 10*20 7c 28 20 20 2f 31 30 29 20 23 a 23 9*20 23 9*20 23 9*20 23 9*20 23 9*20 23 20
  //   53 54 20 7c 10*20 7c 28 20 20 2f 31 30 29 20 23 a 23 9*20 23 9*20 23 9*20 23 9*20 23 9*20 23 20 48
  //   47 20 7c 10*20 7c 28 20 20 2f 31 30 29 20 23 a 23 9*20 23 9*20 23 9*20 23 9*20 23 9*20 23 24*20 23 a
  //   76*23 a 52*20
  //   FFL
  //   contents of rom_2 (hex, n*v repeats v):
  //   0 51*20 a 52*20 a 52*20 a 9*20 34*5f 9*20 a 8*20 7c 34*23 7c 8*20 a 8*20 7c 34*23 7c 8*20 a 8*20 7c
  //   34*23 7c 8*20 a 8*20 7c 34*23 7c 8*20 a 8*20 7c 34*23 7c 8*20 a 8*20 7c 34*23 7c 8*20 a 8*20 7c
  //   34*23 7c 8*20 a 8*20 7c 34*23 7c 8*20 a 8*20 7c 34*23 7c 8*20 a 8*20 7c 34*23 7c 8*20 a 8*20 7c
  //   34*23 7c 8*20 a 8*20 7c 34*23 7c 8*20 a 8*20 7c 34*23 7c 8*20 a 8*20 7c 34*23 7c 8*20 a 8*20 7c
  //   34*23 7c 8*20 a 8*20 7c 34*23 7c 8*20 a 8*20 7c 34*23 7c 8*20 a 8*20 7c 34*23 7c 8*20 a 8*20 7c
  //   34*23 7c 8*20 a 52*20 a 52*20 a 52*20 a 52*20
  //   FFFL
  //   contents of rom_3 (hex, n*v repeats v):
  //   0 51*20 a 52*20 a 52*20 a 52*20 a 52*20 a 52*20 a 52*20 a 18*20 16*5f 18*20 a 17*20 7c 16*23 7c
  //   17*20 a 17*20 7c 16*23 7c 17*20 a 17*20 7c 16*23 7c 17*20 a 17*20 7c 16*23 7c 17*20 a 17*20 7c 16*23
  //   7c 17*20 a 17*20 7c 16*23 7c 17*20 a 17*20 7c 16*23 7c 17*20 a 17*20 7c 16*23 7c 17*20 a 17*20 7c
  //   16*23 7c 17*20 a 17*20 7c 16*23 7c 17*20 a 17*20 7c 16*23 7c 17*20 a 52*20 a 52*20 a 52*20 a 52*20 a
  //   52*20 a 52*20 a 52*20 a 52*20
  //   FFFFL
  //   contents of rom_4 (hex, n*v repeats v):
  //   0 51*20 a 52*20 a 52*20 a 52*20 a 52*20 a 52*20 a 52*20 a 52*20 a 52*20 a 52*20 a 24*20 4*5f 24*20 a
  //   23*20 7c 4*23 7c 23*20 a 23*20 7c 4*23 7c 23*20 a 23*20 7c 4*23 7c 23*20 a 23*20 7c 4*23 7c 23*20 a
  //   23*20 7c 4*23 7c 23*20 a 52*20 a 52*20 a 52*20 a 52*20 a 52*20 a 52*20 a 52*20 a 52*20 a 52*20 a
  //   52*20 a 52*20
  //   LFL
  //   contents of rom_5 (hex, n*v repeats v):
  //   0 5c 5f 49*20 a 23 23 5c 5f 48*20 a 4*23 5c 5f 46*20 a 6*23 5c 5f 44*20 a 8*23 7c 43*20 a 8*23 7c
  //   43*20 a 8*23 7c 43*20 a 8*23 7c 43*20 a 8*23 7c 43*20 a 8*23 7c 43*20 a 8*23 7c 43*20 a 8*23 7c
  //   43*20 a 8*23 7c 43*20 a 8*23 7c 43*20 a 8*23 7c 43*20 a 8*23 7c 43*20 a 8*23 7c 43*20 a 8*23 7c
  //   43*20 a 8*23 7c 43*20 a 8*23 7c 43*20 a 8*23 7c 43*20 a 8*23 7c 43*20 a 8*23 7c 43*20 a 6*23 2f
  //   45*20 a 4*23 2f 47*20 a 23 23 2f 49*20 a 2f 51*20
  //   LFFL
  //   contents of rom_6 (hex, n*v repeats v):
  //   0 51*20 a 52*20 a 52*20 a 8*5f 44*20 a 8*23 7c 43*20 a 8*23 7c 43*20 a 8*23 7c 43*20 a 8*23 7c 43*20
  //   a 8*23 7c 43*20 a 8*23 7c 43*20 a 8*23 7c 43*20 a 8*23 7c 43*20 a 8*23 7c 43*20 a 8*23 7c 43*20 a
  //   8*23 7c 43*20 a 8*23 7c 43*20 a 8*23 7c 43*20 a 8*23 7c 43*20 a 8*23 7c 43*20 a 8*23 7c 43*20 a 8*23
  //   7c 43*20 a 8*23 7c 43*20 a 8*23 7c 43*20 a 52*20 a 52*20 a 52*20 a 52*20
  //   LFFFL
  //   contents of rom_7 (hex, n*v repeats v):
  //   0 51*20 a 52*20 a 52*20 a 52*20 a 52*20 a 52*20 a 52*20 a 17*5f 35*20 a 17*23 7c 34*20 a 17*23 7c
  //   34*20 a 17*23 7c 34*20 a 17*23 7c 34*20 a 17*23 7c 34*20 a 17*23 7c 34*20 a 17*23 7c 34*20 a 17*23
  //   7c 34*20 a 17*23 7c 34*20 a 17*23 7c 34*20 a 17*23 7c 34*20 a 52*20 a 52*20 a 52*20 a 52*20 a 52*20
  //   a 52*20 a 52*20 a 52*20
  //   LFFFFL
  //   contents of rom_8 (hex, n*v repeats v):
  //   0 51*20 a 52*20 a 52*20 a 52*20 a 52*20 a 52*20 a 52*20 a 52*20 a 52*20 a 52*20 a 18*20 5*5f 29*20 a
  //   17*20 7c 5*23 7c 28*20 a 17*20 7c 5*23 7c 28*20 a 17*20 7c 5*23 7c 28*20 a 17*20 7c 5*23 7c 28*20 a
  //   17*20 7c 5*23 7c 28*20 a 52*20 a 52*20 a 52*20 a 52*20 a 52*20 a 52*20 a 52*20 a 52*20 a 52*20 a
  //   52*20 a 52*20
  //   RFL
  //   contents of rom_9 (hex, n*v repeats v):
  //   0 50*20 5f 2f a 48*20 5f 2f 23 23 a 46*20 5f 2f 4*23 a 44*20 5f 2f 6*23 a 43*20 7c 8*23 a 43*20 7c
  //   8*23 a 43*20 7c 8*23 a 43*20 7c 8*23 a 43*20 7c 8*23 a 43*20 7c 8*23 a 43*20 7c 8*23 a 43*20 7c 8*23
  //   a 43*20 7c 8*23 a 43*20 7c 8*23 a 43*20 7c 8*23 a 43*20 7c 8*23 a 43*20 7c 8*23 a 43*20 7c 8*23 a
  //   43*20 7c 8*23 a 43*20 7c 8*23 a 43*20 7c 8*23 a 43*20 7c 8*23 a 43*20 7c 8*23 a 45*20 5c 6*23 a
  //   47*20 5c 4*23 a 49*20 5c 23 23 a 51*20 5c
  //   RFFL
  //   contents of rom_10 (hex, n*v repeats v):
  //   0 51*20 a 52*20 a 52*20 a 52*20 a 41*20 5f 2f 7c 8*20 a 39*20 5f 2f 23 23 7c 8*20 a 37*20 5f 2f 4*23
  //   7c 8*20 a 35*20 5f 2f 6*23 7c 8*20 a 34*20 7c 8*23 7c 8*20 a 34*20 7c 8*23 7c 8*20 a 34*20 7c 8*23
  //   7c 8*20 a 34*20 7c 8*23 7c 8*20 a 34*20 7c 8*23 7c 8*20 a 34*20 7c 8*23 7c 8*20 a 34*20 7c 8*23 7c
  //   8*20 a 34*20 7c 8*23 7c 8*20 a 34*20 7c 8*23 7c 8*20 a 34*20 7c 8*23 7c 8*20 a 34*20 7c 8*23 7c 8*20
  //   a 36*20 5c 6*23 7c 8*20 a 38*20 5c 4*23 7c 8*20 a 40*20 5c 23 23 7c 8*20 a 42*20 5c 7c 8*20 a 52*20
  //   a 52*20 a 52*20 a 52*20
  //   RFFFL
  //   contents of rom_11 (hex, n*v repeats v):
  //   0 51*20 a 52*20 a 52*20 a 52*20 a 52*20 a 52*20 a 52*20 a 35*20 17*5f a 34*20 7c 17*23 a 34*20 7c
  //   17*23 a 34*20 7c 17*23 a 34*20 7c 17*23 a 34*20 7c 17*23 a 34*20 7c 17*23 a 34*20 7c 17*23 a 34*20
  //   7c 17*23 a 34*20 7c 17*23 a 34*20 7c 17*23 a 34*20 7c 17*23 a 52*20 a 52*20 a 52*20 a 52*20 a 52*20
  //   a 52*20 a 52*20 a 52*20
  //   RFFFFL
  //   contents of rom_12 (hex, n*v repeats v):
  //   0 51*20 a 52*20 a 52*20 a 52*20 a 52*20 a 52*20 a 52*20 a 52*20 a 52*20 a 52*20 a 29*20 5*5f 18*20 a
  //   28*20 7c 5*23 7c 17*20 a 28*20 7c 5*23 7c 17*20 a 28*20 7c 5*23 7c 17*20 a 28*20 7c 5*23 7c 17*20 a
  //   28*20 7c 5*23 7c 17*20 a 52*20 a 52*20 a 52*20 a 52*20 a 52*20 a 52*20 a 52*20 a 52*20 a 52*20 a
  //   52*20 a 52*20
  //   FRFL
  //   contents of rom_13 (hex, n*v repeats v):
  //   0 51*20 a 52*20 a 52*20 a 52*20 a 41*20 5f 2f 7c 8*20 a 39*20 5f 2f 23 23 7c 8*20 a 37*20 5f 2f 4*23
  //   7c 8*20 a 35*20 5f 2f 6*23 7c 8*20 a 34*20 7c 8*23 7c 8*20 a 34*20 7c 8*23 7c 8*20 a 34*20 7c 8*23
  //   7c 8*20 a 34*20 7c 8*23 7c 8*20 a 34*20 7c 8*23 7c 8*20 a 34*20 7c 8*23 7c 8*20 a 34*20 7c 8*23 7c
  //   8*20 a 34*20 7c 8*23 7c 8*20 a 34*20 7c 8*23 7c 8*20 a 34*20 7c 8*23 7c 8*20 a 34*20 7c 8*23 7c 8*20
  //   a 36*20 5c 6*23 7c 8*20 a 38*20 5c 4*23 7c 8*20 a 40*20 5c 23 23 7c 8*20 a 42*20 5c 7c 8*20 a 52*20
  //   a 52*20 a 52*20 a 52*20
  //   FLFL
  //   contents of rom_14 (hex, n*v repeats v):
  //   0 51*20 a 52*20 a 52*20 a 52*20 a 8*20 7c 5c 5f 41*20 a 8*20 7c 23 23 5c 5f 39*20 a 8*20 7c 4*23 5c
  //   5f 37*20 a 8*20 7c 6*23 5c 5f 35*20 a 8*20 7c 8*23 7c 34*20 a 8*20 7c 8*23 7c 34*20 a 8*20 7c 8*23
  //   7c 34*20 a 8*20 7c 8*23 7c 34*20 a 8*20 7c 8*23 7c 34*20 a 8*20 7c 8*23 7c 34*20 a 8*20 7c 8*23 7c
  //   34*20 a 8*20 7c 8*23 7c 34*20 a 8*20 7c 8*23 7c 34*20 a 8*20 7c 8*23 7c 34*20 a 8*20 7c 8*23 7c
  //   34*20 a 8*20 7c 6*23 2f 36*20 a 8*20 7c 4*23 2f 38*20 a 8*20 7c 23 23 2f 40*20 a 8*20 7c 2f 42*20 a
  //   52*20 a 52*20 a 52*20 a 52*20
  //   FFRFL
  //   contents of rom_15 (hex, n*v repeats v):
  //   0 51*20 a 52*20 a 52*20 a 52*20 a 52*20 a 52*20 a 52*20 a 52*20 a 32*20 5f 2f 7c 17*20 a 30*20 5f 2f
  //   23 23 7c 17*20 a 29*20 2f 4*23 7c 17*20 a 28*20 7c 5*23 7c 17*20 a 28*20 7c 5*23 7c 17*20 a 28*20 7c
  //   5*23 7c 17*20 a 28*20 7c 5*23 7c 17*20 a 28*20 7c 5*23 7c 17*20 a 29*20 5c 4*23 7c 17*20 a 31*20 5c
  //   23 23 7c 17*20 a 33*20 5c 7c 17*20 a 52*20 a 52*20 a 52*20 a 52*20 a 52*20 a 52*20 a 52*20 a 52*20
  //   FFLFL
  //   contents of rom_16 (hex, n*v repeats v):
  //   0 51*20 a 52*20 a 52*20 a 52*20 a 52*20 a 52*20 a 52*20 a 52*20 a 17*20 7c 5c 5f 32*20 a 17*20 7c 23
  //   23 5c 5f 30*20 a 17*20 7c 4*23 5c 29*20 a 17*20 7c 5*23 7c 28*20 a 17*20 7c 5*23 7c 28*20 a 17*20 7c
  //   5*23 7c 28*20 a 17*20 7c 5*23 7c 28*20 a 17*20 7c 5*23 7c 28*20 a 17*20 7c 4*23 2f 29*20 a 17*20 7c
  //   23 23 2f 31*20 a 17*20 7c 2f 33*20 a 52*20 a 52*20 a 52*20 a 52*20 a 52*20 a 52*20 a 52*20 a 52*20
  //   contents of rom_17 (hex, n*v repeats v):
  //   0 76*23 a 23 74*20 23 a 23 74*20 23 a 23 74*20 23 a 23 26*20 5*5f 20 20 5f 40*20 23 a 23 25*20 7c 5f
  //   20 20 20 5f 7c 7c 20 7c 39*20 23 a 23 27*20 7c 20 7c 20 20 7c 20 7c 5f 5f 4*20 5f 5f 5f 30*20 23 a
  //   23 27*20 7c 20 7c 20 20 7c 20 27 5f 20 5c 20 20 2f 20 5f 20 5c 29*20 23 a 23 27*20 7c 20 7c 20 20 7c
  //   20 7c 20 7c 20 7c 7c 20 20 5f 5f 2f 29*20 23 a 23 27*20 5c 5f 2f 20 20 7c 5f 7c 20 7c 5f 7c 20 5c 5f
  //   5f 5f 7c 29*20 23 a 23 20 5f 5f 5f 20 20 5f 5f 5f 8*20 5f 7*20 5f 7*20 5f 40*20 23 a 23 20 7c 20 20
  //   5c 2f 20 20 7c 7*20 7c 20 7c 5*20 28 20 29 5*20 7c 20 7c 39*20 23 a 23 20 7c 20 2e 20 20 2e 20 7c 20
  //   20 5f 5f 5f 20 20 7c 20 7c 20 20 5f 5f 5f 7c 2f 20 5f 5f 5f 20 20 7c 20 7c 5f 5f 20 20 20 5f 20 20
  //   20 5f 20 20 5f 20 5f 5f 20 20 5f 20 5f 5f 20 20 5f 5f 5f 20 5f 5f 6*20 5f 5f 20 23 a 23 20 7c 20 7c
  //   5c 2f 7c 20 7c 20 2f 20 5f 20 5c 20 7c 20 7c 20 2f 20 5f 20 5c 20 2f 20 5f 5f 7c 20 7c 20 27 5f 20
  //   5c 20 7c 20 7c 20 7c 20 7c 7c 20 27 5f 5f 7c 7c 20 27 5f 5f 7c 2f 20 5f 20 5c 5c 20 5c 20 2f 5c 20
  //   2f 20 2f 20 23 a 23 20 7c 20 7c 20 20 7c 20 7c 7c 20 28 5f 29 20 7c 7c 20 7c 7c 20 20 5f 5f 2f 20 5c
  //   5f 5f 20 5c 20 7c 20 7c 5f 29 20 7c 7c 20 7c 5f 7c 20 7c 7c 20 7c 20 20 20 7c 20 7c 20 20 7c 20 28
  //   5f 29 20 7c 5c 20 56 20 20 56 20 2f 20 20 23 a 23 20 5c 5f 7c 20 20 7c 5f 2f 20 5c 5f 5f 5f 2f 20 7c
  //   5f 7c 20 5c 5f 5f 5f 7c 20 7c 5f 5f 5f 2f 20 7c 5f 2e 5f 5f 2f 20 20 5c 5f 5f 2c 5f 7c 7c 5f 7c 20
  //   20 20 7c 5f 7c 20 20 20 5c 5f 5f 5f 2f 20 20 5c 5f 2f 5c 5f 2f 20 20 20 23 a 23 74*20 23 a 23 74*20
  //   23 a 23 74*20 23 a 23 74*20 23 a 23 74*20 23 a 23 74*20 23 a 23 74*20 23 a 23 74*20 23 a 23 74*20 23
  //   a 23 74*20 23 a 23 74*20 23 a 23 74*20 23 a 23 74*20 23 a 23 74*20 23 a 23 74*20 23 a 23 74*20 23 a
  //   23 74*20 23 a 23 39*20 50 52 45 53 53 20 41 4e 59 20 4b 45 59 20 54 4f 20 43 4f 4e 54 49 4e 55 45 2e
  //   2e 2e 7*20 23 a 23 74*20 23 a 76*23 a 52*20
  //   contents of rom_18 (hex, n*v repeats v):
  //   0 76*23 a 23 74*20 23 a 23 74*20 23 a 23 74*20 23 a 23 74*20 23 a 23 74*20 23 a 23 74*20 23 a 23
  //   74*20 23 a 23 74*20 23 a 23 9*20 7c 14*20 7c 13*20 7c 24*20 7c 20 28 20 20 7c 20 20 29 20 20 23 a 23
  //   74*20 23 a 23 74*20 23 a 23 74*20 23 a 23 74*20 23 a 23 74*20 23 a 23 74*20 23 a 23 74*20 23 a 23
  //   74*20 23 a 23 74*20 23 a 23 4*20 65*2d 5*20 23 a 23 74*20 23 a 23 20*20 5e 24*20 2e 28*20 23 a 23
  //   8*20 2e 19*20 2e 10*20 2e 18*20 2e 7*20 2e 7*20 23 a 23 16*20 2e 17*20 2e 17*20 5e 7*20 2e 13*20 23
  //   a 23 23*20 2e 18*20 2e 31*20 23 a 23 6*20 2e 6*20 5e 16*20 5e 23*20 2e 19*20 23 a 23 23*20 2e 11*20
  //   2e 5*20 2e 20*20 5e 11*20 23 a 23 74*20 23 a 76*23 a 23 74*20 23 a 76*23 a 23 9*20 23 9*20 23 9*20
  //   23 9*20 23 9*20 23 20 48 50 20 7c 10*20 7c 28 20 20 2f 31 30 29 20 23 a 23 9*20 23 9*20 23 9*20 23
  //   9*20 23 9*20 23 20 53 54 20 7c 10*20 7c 28 20 20 2f 31 30 29 20 23 a 23 9*20 23 9*20 23 9*20 23 9*20
  //   23 9*20 23 20 48 47 20 7c 10*20 7c 28 20 20 2f 31 30 29 20 23 a 23 9*20 23 9*20 23 9*20 23 9*20 23
  //   9*20 23 24*20 23 a 76*23 a 52*20
  //   START SCREEN
  //   ATACK BOARD
endmodule

// Maps
module maps (
  input  [7:0] ADDR,
  input  [11:0] ELEM,
  output [11:0] Width,
  output [11:0] Height,
  output [7:0] Xpp,
  output [7:0] Ypp,
  output [7:0] DATA,
  output [11:0] LEN
);

  wire [7:0] mgeD0, undriven_4, undriven_5;
  wire [11:0] undriven, undriven_2, undriven_3;

  ROM #(.addrWidth(12)) rom_1 (.addr(ELEM), .data(mgeD0));  // open: sel
  Multiplexer #(.select(5), .width(8), .enable("false")) multiplexer_1 (
    .in0(mgeD0), .out(DATA), .sel(ADDR[4:0]));  // open: in1, in2, in3, in4, in5, in6, in7, in8, in9, in10, in11, in12, in13, in14, in15, in16, in17, in18, in19, in20, in21, in22, in23, in24, in25, in26, in27, in28, in29, in30, in31
  Multiplexer #(.select(5), .width(12), .enable("false")) multiplexer_2 (
    .in0(12'h99), .in30(undriven), .in31(undriven), .out(LEN), .sel(ADDR[4:0]));  // open: in1, in2, in3, in4, in5, in6, in7, in8, in9, in10, in11, in12, in13, in14, in15, in16, in17, in18, in19, in20, in21, in22, in23, in24, in25, in26, in27, in28, in29
  Multiplexer #(.select(5), .width(12), .enable("false")) multiplexer_3 (
    .in0(12'hb), .in30(undriven_2), .in31(undriven_2), .out(Width), .sel(ADDR[4:0]));  // open: in1, in2, in3, in4, in5, in6, in7, in8, in9, in10, in11, in12, in13, in14, in15, in16, in17, in18, in19, in20, in21, in22, in23, in24, in25, in26, in27, in28, in29
  Multiplexer #(.select(5), .width(12), .enable("false")) multiplexer_4 (
    .in0(12'h8), .in30(undriven_3), .in31(undriven_3), .out(Height), .sel(ADDR[4:0]));  // open: in1, in2, in3, in4, in5, in6, in7, in8, in9, in10, in11, in12, in13, in14, in15, in16, in17, in18, in19, in20, in21, in22, in23, in24, in25, in26, in27, in28, in29
  Multiplexer #(.select(5), .width(8), .enable("false")) multiplexer_5 (
    .in0(8'h3), .in30(undriven_4), .in31(undriven_4), .out(Xpp), .sel(ADDR[4:0]));  // open: in1, in2, in3, in4, in5, in6, in7, in8, in9, in10, in11, in12, in13, in14, in15, in16, in17, in18, in19, in20, in21, in22, in23, in24, in25, in26, in27, in28, in29
  Multiplexer #(.select(5), .width(8), .enable("false")) multiplexer_6 (
    .in0(8'h3), .in30(undriven_5), .in31(undriven_5), .out(Ypp), .sel(ADDR[4:0]));  // open: in1, in2, in3, in4, in5, in6, in7, in8, in9, in10, in11, in12, in13, in14, in15, in16, in17, in18, in19, in20, in21, in22, in23, in24, in25, in26, in27, in28, in29

  // Other names for the same wires on the sheet: mdeMux1[7:0] = DATA; mdeMuxl1[11:0] = LEN; mgeAddr1[4:0] = ADDR[4:0];
  //   mgeEl[11:0] = ELEM; mhMuxl1[11:0] = Height; mwMuxl1[11:0] = Width; mXMuxl1[7:0] = Xpp; mYMuxl1[7:0] = Ypp

  // Notes on the sheet:
  //   TEST MAP
  //   contents of rom_1 (hex, n*v repeats v):
  //   0 4 3 2 36*23 20 66 6a 61 20 6*23 20 23 23 20 32 6*23 20 20 23 23 20 36*23
endmodule

module printing_map (
  input  [7:0] Curr_char,
  input  [7:0] height_of_map,
  input  [7:0] length_of_map,
  input  in_4
);

  wire button_1_out, comparator_1_eq, comparator_2_eq, comparator_3_eq, comparator_3_lt;
  wire [7:0] adder_1_out, controlled_buffer_1_out, register_1_q, register_2_q;

  Register register_1 (.D(adder_1_out), .Q(register_1_q), .clk(in_4), .clr(button_1_out));  // open: en
  Adder adder_1 (.a(register_1_q), .b(8'h1), .out(adder_1_out));  // open: cin, cout
  Button button_1 (.out(button_1_out));
  Comparator comparator_1 (.a(8'h1), .b(register_1_q), .eq(comparator_1_eq));  // open: gt, lt
  Comparator comparator_2 (.a(8'h2), .b(register_1_q), .eq(comparator_2_eq));  // open: gt, lt
  Comparator comparator_3 (.a(8'h3), .b(register_1_q), .eq(comparator_3_eq), .lt(comparator_3_lt));  // open: gt
  Register y (.D(Curr_char), .en(comparator_1_eq), .clk(in_4));  // open: Q, clr
  Register x (.D(Curr_char), .en(comparator_2_eq), .clk(in_4));  // open: Q, clr
  Register Direction (.D(Curr_char), .en(comparator_3_eq), .clk(in_4));  // open: Q, clr
  assign controlled_buffer_1_out = comparator_3_lt ? Curr_char : 8'bz;  // Controlled_Buffer controlled_buffer_1
  Register register_2 (.D(controlled_buffer_1_out), .Q(register_2_q), .clk(in_4));  // open: en, clr

  // Other names for the same wires on the sheet: Clock = in_4; height[7:0] = height_of_map;
  //   length[7:0] = length_of_map
endmodule

module x_y__to_memory_elem_number (
  input  [11:0] H,
  input  [7:0] Y,
  input  [7:0] X,
  input  [11:0] START,
  output [11:0] ELEM
);

  wire [11:0] adder_1_out, bit_extender_1_out, bit_extender_2_out, multiplier_1_out;

  assign bit_extender_1_out = {{4{1'b0}}, Y};  // Bit_Extender bit_extender_1
  Multiplier #(.width(12)) multiplier_1 (.a(H), .b(bit_extender_1_out), .out(multiplier_1_out));  // open: cin, cout
  assign bit_extender_2_out = {{4{1'b0}}, X};  // Bit_Extender bit_extender_2
  Adder #(.width(12)) adder_1 (.a(multiplier_1_out), .b(bit_extender_2_out), .out(adder_1_out));  // open: cin, cout
  Adder #(.width(12)) adder_2 (.a(adder_1_out), .b(START), .out(ELEM));  // open: cin, cout
endmodule

module enemies (
  input  [1:0] ADDR,
  input  [7:0] ELEMIm,
  input  [7:0] ELEMNm,
  output [7:0] Img,
  output [7:0] Txt,
  output [7:0] HP,
  output [7:0] DMG
);

  wire [7:0] EnImEl1, EnImEl1txt, EnImEl2, EnImEl2txt, EnImEl3, EnImEl3txt, EnImEl4, EnImEl4txt;

  ROM rom_1 (.addr(ELEMIm), .data(EnImEl1));  // open: sel
  ROM rom_2 (.addr(ELEMIm), .data(EnImEl2));  // open: sel
  ROM rom_3 (.addr(ELEMIm), .data(EnImEl3));  // open: sel
  ROM rom_4 (.addr(ELEMIm), .data(EnImEl4));  // open: sel
  Multiplexer #(.select(2), .width(8), .enable("false")) multiplexer_1 (
    .in0(EnImEl1), .in1(EnImEl2), .in2(EnImEl3), .in3(EnImEl4), .out(Img), .sel(ADDR));
  Multiplexer #(.select(2), .width(8), .enable("false")) multiplexer_2 (
    .in0(EnImEl1txt), .in1(EnImEl2txt), .in2(EnImEl3txt), .in3(EnImEl4txt), .out(Txt), .sel(ADDR));
  Multiplexer #(.select(2), .width(8), .disabled(0), .enable("false")) multiplexer_3 (
    .in0(8'h24), .in1(8'h12), .in2(8'h62), .in3(8'h36), .out(HP), .sel(ADDR));
  Multiplexer #(.select(2), .width(8), .disabled(0), .enable("false")) multiplexer_4 (
    .in0(8'h5), .in1(8'h3), .in2(8'h24), .in3(8'h12), .out(DMG), .sel(ADDR));
  ROM rom_5 (.addr(ELEMIm), .data(EnImEl1txt));  // open: sel
  ROM rom_6 (.addr(ELEMIm), .data(EnImEl2txt));  // open: sel
  ROM rom_7 (.addr(ELEMIm), .data(EnImEl3txt));  // open: sel
  ROM rom_8 (.addr(ELEMIm), .data(EnImEl4txt));  // open: sel

  // Other names for the same wires on the sheet: enaddr1[1:0] = ADDR; EnImEl[7:0] = ELEMIm; EnImEltxt[7:0] = ELEMNm

  // Notes on the sheet:
  //   rat
  //   mouse
  //   ferret
  //   snake
  //   contents of rom_1 (hex, n*v repeats v):
  //   15*20 35 64 6d 67 2e 9*20 2f 5c 5f 2f 5c 16*20 28 20 6f 20 6f 20 29 15*20 2f 20 20 56 20 20 5c 15*20
  //   2f 20 3e 20 20 3c 20 20 5c 12*20 28 20 2f 5*20 5c 20 29 20 20 20 7c 8*20 5c 5f 20 4*2d 20 5f 2f 5f
  //   5f 5f 2f 24*20
  //   contents of rom_2 (hex, n*v repeats v):
  //   13*20 33 64 6d 67 2e 13*20 2f 5e 5c 5e 5c 5f 10*20 2f 4*20 7c 5*20 6f 5c 5f 7*20 7c 4*20 2f 7*20 5f
  //   2f 7*20 5c 20 20 20 2f 6*20 5f 5f 3e 9*20 5c 5f 5f 7c 20 20 20 5f 5f 5f 29 14*20 5c 5f 5f 5f 7c 5c
  //   5f 5f 30*20
  //   contents of rom_3 (hex, n*v repeats v):
  //   14*20 32 30 64 6d 67 2e 8*20 2f 29 5*5f 28 5c 12*20 28 2f 20 6f 20 20 20 6f 20 5c 29 11*20 7c 4*20
  //   4f 4*20 7c 12*20 5c 20 20 2d 5e 2d 20 20 2f 13*20 2f 7*20 5c 12*20 7c 9*20 7c 28*20
  //   contents of rom_4 (hex, n*v repeats v):
  //   14*20 31 30 64 6d 67 2e 4*20 2e 2d 2e 17*20 3e 2d 30 5f 30 29 29 20 20 7c 20 20 2f 20 29 11*20 2f 2f
  //   20 20 20 7c 2e 2f 5f 5f 29 10*20 28 28 5f 2e 2d 2d 27 20 5f 20 20 27 2e 10*20 60 2d 5f 5f 2d 2d 27
  //   20 27 2d 2e 20 29 16*20 5f 5f 2d 2d 27 28*20
  //   rat
  //   mouse
  //   ferret
  //   snake
  //   8x22 = 176
  //   20 chars name len
  //   contents of rom_5 (hex, n*v repeats v):
  //   6*20 53 43 41 52 59 20 52 41 54 5*20
  //   contents of rom_6 (hex, n*v repeats v):
  //   5*20 45 56 49 4c 20 4d 4f 55 53 45 5*20
  //   contents of rom_7 (hex, n*v repeats v):
  //   4*20 43 55 54 45 20 46 45 52 52 45 54 5*20
  //   contents of rom_8 (hex, n*v repeats v):
  //   4*20 4c 49 54 54 4c 45 20 53 4e 41 4b 45 4*20
endmodule

module quick (
  input  IN,
  output OUT
);

  wire not_1_out, not_2_out;

  not not_1 (not_1_out, IN);
  Register #(.width(1)) register_1 (.D(IN), .Q(OUT), .clk(IN), .clr(not_2_out));  // open: en
  not not_2 (not_2_out, not_1_out);
endmodule

module food (
  input  [7:0] FOOD,
  output [7:0] GIVEHP
);

  wire [1:0] bit_extender_1_out;
  wire [7:0] subtractor_1_out;

  Subtractor subtractor_1 (.a(FOOD), .b(8'h61), .out(subtractor_1_out));  // open: bin, bout
  Multiplexer #(.select(2), .width(8), .enable("false")) multiplexer_1 (
    .in0(8'h5), .in1(8'h3), .in2(8'h7), .in3(8'ha), .out(GIVEHP), .sel(bit_extender_1_out));
  Bit_Extender #(.out_width(2)) bit_extender_1 (.in(subtractor_1_out), .out(bit_extender_1_out));

  // Notes on the sheet:
  //   const/2
endmodule

module Lquick (
  input  IN,
  input  CLC,
  output OUT
);

  wire and_1_out, comparator_1_eq, quick_1_out;
  wire [2:0] adder_1_out, register_1_q;

  and and_1 (and_1_out, CLC, ~comparator_1_eq);  // AND_Gate
  quick quick_1 (.IN(IN), .OUT(quick_1_out));
  Adder #(.width(3)) adder_1 (.a(3'b001), .b(register_1_q), .out(adder_1_out));  // open: cin, cout
  Comparator #(.width(3), .mode("unsigned")) comparator_1 (
    .a(3'b111), .b(register_1_q), .gt(OUT), .eq(comparator_1_eq));  // open: lt
  Register #(.width(3)) register_1 (.D(adder_1_out), .Q(register_1_q), .clk(and_1_out), .clr(quick_1_out));  // open: en
endmodule

module weapon (
  input  GenRnd,
  input  [7:0] WEAPON,
  output [7:0] DMG
);

  wire random_1_out;
  wire [2:0] bit_extender_1_out;
  wire [7:0] bit_extender_2_out, multiplexer_1_out, subtractor_1_out;

  Subtractor subtractor_1 (.a(WEAPON), .b(8'h66), .out(subtractor_1_out));  // open: bin, bout
  Multiplexer #(.select(3), .width(8), .enable("false")) multiplexer_1 (
    .in0(8'h5), .in1(8'h14), .in2(8'hf), .in3(8'ha), .in4({8{1'b1}}), .out(multiplexer_1_out),
    .sel(bit_extender_1_out));  // open: in5, in6, in7
  Bit_Extender #(.out_width(3)) bit_extender_1 (.in(subtractor_1_out), .out(bit_extender_1_out));
  Random #(.width(1)) random_1 (.clk(GenRnd), .out(random_1_out));  // open: next, clr
  assign bit_extender_2_out = {{7{1'b0}}, random_1_out};  // Bit_Extender bit_extender_2
  Adder adder_1 (.a(bit_extender_2_out), .b(multiplexer_1_out), .out(DMG));  // open: cin, cout
endmodule
